// Logisim project Ctl_Opcode_Decoder.circ as structural Verilog: 1 circuit, main circuit Opcode_Decoder
module Opcode_Decoder (
  input  [5:0] Opcode,
  output Shift,
  output Data_Processing,
  output Load_Store,
  output SP_Address,
  output Conditional
);

  wire and_1_out, and_2_out;

  and and_1 (and_1_out, Opcode[5], Opcode[4], ~Opcode[3], Opcode[2]);  // AND_Gate
  and and_2 (and_2_out, Opcode[5], Opcode[4], Opcode[3], ~Opcode[2], ~Opcode[1]);  // AND_Gate
  and and_3 (Shift, ~Opcode[5], ~Opcode[4]);  // AND_Gate
  and and_4 (Data_Processing, ~Opcode[5], Opcode[4], ~Opcode[3], ~Opcode[2], ~Opcode[1], ~Opcode[0]);  // AND_Gate
  and and_5 (Load_Store, Opcode[5], ~Opcode[4], ~Opcode[3], Opcode[2]);  // AND_Gate
  and and_6 (SP_Address, Opcode[5], ~Opcode[4], Opcode[3], Opcode[2]);  // AND_Gate
  or or_1 (Conditional, and_1_out, and_2_out);
endmodule
