// Logisim project Ctl_Shift_Add_Sub_Mov.circ as structural Verilog: 5 circuits, main circuit Shift_Add_Sub_Mov
module Shift_Add_Sub_Mov (
  input  Enable,
  input  [15:0] Instruction,
  output [3:0] Flags_Update_Mask,
  output Carry,
  output Imm32_Enable,
  output [2:0] Rm,
  output [2:0] Rn,
  output [2:0] Rd,
  output [4:0] Imm5,
  output [31:0] Imm32,
  output [3:0] ALU_Opcode
);

  wire and_1_out, isADDSUB, isMOV, isSHIFT, not_1_out, useIMM3, useIMM32;
  wire [1:0] priorityEncoder;
  wire [2:0] Rd_t;
  wire [3:0] ALUOp, Flags, multiplexer_12_out, multiplexer_13_out;
  wire [7:0] negator_1_out;
  wire [31:0] bit_extender_1_out, bit_extender_2_out, Imm32_t;

  Multiplexer #(.width(3)) multiplexer_1 (.in0(Instruction[2:0]), .in1(Instruction[10:8]), .out(Rd_t), .sel(isMOV));
  Priority_Encoder #(.select(2)) priority_encoder_1 (
    .in0(isMOV), .in1(isSHIFT), .in2(isADDSUB), .in3(1'b0), .out(priorityEncoder));  // open: gs, en_out, en_in
  is_SHIFT is_shift_1 (.inSHIFT(Instruction[15:13]), .outSHIFT(isSHIFT));
  is_MOVS is_movs_1 (.InIsMov(Instruction[15:13]), .isMov(isMOV));
  is_ADD_SUB is_add_sub_1 (.inADDSUB(Instruction[15:11]), .outADDSUB(isADDSUB));
  Multiplexer #(.select(2), .width(4)) multiplexer_2 (
    .in0(4'b1100), .in1(4'b1110), .in2(4'b1111), .in3(4'b0000), .out(Flags), .sel(priorityEncoder));
  not not_1 (not_1_out, Enable);
  and and_1 (and_1_out, Instruction[9], isADDSUB);
  use_IMM3 use_imm3_1 (.is_ADD_SUB(isADDSUB), .is_10thBit(Instruction[10]), .outIsIMM3(useIMM3));
  Multiplexer #(.width(4)) multiplexer_3 (.in0(Flags), .in1(4'b0000), .out(Flags_Update_Mask), .sel(not_1_out));
  Multiplexer multiplexer_4 (.in0(and_1_out), .in1(1'b0), .out(Carry), .sel(not_1_out));
  Multiplexer multiplexer_5 (.in0(useIMM32), .in1(1'b0), .out(Imm32_Enable), .sel(not_1_out));
  Multiplexer #(.width(3)) multiplexer_6 (.in0(Instruction[8:6]), .in1(3'b000), .out(Rm), .sel(not_1_out));
  Multiplexer #(.width(3)) multiplexer_7 (.in0(Instruction[5:3]), .in1(3'b000), .out(Rn), .sel(not_1_out));
  Multiplexer #(.width(3)) multiplexer_8 (.in0(Rd_t), .in1(3'b000), .out(Rd), .sel(not_1_out));
  Multiplexer #(.width(5)) multiplexer_9 (.in0(Instruction[10:6]), .in1({5{1'b0}}), .out(Imm5), .sel(not_1_out));
  Multiplexer #(.width(32)) multiplexer_10 (.in0(Imm32_t), .in1({32{1'b0}}), .out(Imm32), .sel(not_1_out));
  Multiplexer #(.width(4)) multiplexer_11 (.in0(ALUOp), .in1(4'b0000), .out(ALU_Opcode), .sel(not_1_out));
  Multiplexer #(.select(2), .width(4)) multiplexer_12 (
    .in0(4'b0010), .in1(4'b0011), .in2(4'b0100), .out(multiplexer_12_out), .sel(Instruction[12:11]));  // open: in3
  Multiplexer #(.width(4)) multiplexer_13 (
    .in0(4'b0101), .in1(4'b0110), .out(multiplexer_13_out), .sel(Instruction[9]));
  assign bit_extender_1_out = {{29{1'b0}}, Instruction[8:6]};  // Bit_Extender bit_extender_1
  assign bit_extender_2_out = {{24{negator_1_out[7]}}, negator_1_out};  // Bit_Extender bit_extender_2
  Negator negator_1 (.in(Instruction[7:0]), .out(negator_1_out));
  Multiplexer #(.select(2), .width(4)) multiplexer_14 (
    .in0(4'b1001), .in1(multiplexer_12_out), .in2(multiplexer_13_out), .out(ALUOp), .sel(priorityEncoder));  // open: in3
  Multiplexer #(.width(32)) multiplexer_15 (
    .in0(bit_extender_1_out), .in1(bit_extender_2_out), .out(Imm32_t), .sel(useIMM32));
  or or_1 (useIMM32, isMOV, useIMM3);

  // Other names for the same wires on the sheet: Imm8[7:0] = Instruction[7:0]; Rn_t[2:0] = Instruction[5:3];
  //   Imm3[2:0] = Instruction[8:6]; Imm5_t[4:0] = Instruction[10:6]; Rm_t[2:0] = Instruction[8:6];
  //   isSUB = Instruction[9]; tenthBit = Instruction[10]; code[4:0] = Instruction[15:11];
  //   opCodeShift[1:0] = Instruction[12:11]

  // Notes on the sheet:
  //   Note: ALU uses Rn register for shifts. Use Rn instead of Rm for shifts (immediate) here too
  //   Note 3: Imm32_Enable forces the use of the immediate for Rm register
  //   Note 2: MOV uses RSB ALU opcode with Imm8 reversed so that it is copied to output register
  //   Pull output low on Enable = 0
  //   only ADD and SUB use Rm
  //   Enable carry for SUB since it is reversed in ALU
  //   ALU will use Imm32 instead of Rm
endmodule

module is_MOVS (
  input  [2:0] InIsMov,
  output isMov
);

  wire not_1_out, not_2_out;

  not not_1 (not_1_out, InIsMov[2]);
  not not_2 (not_2_out, InIsMov[1]);
  and and_1 (isMov, not_1_out, not_2_out, InIsMov[0]);
endmodule

module is_ADD_SUB (
  input  [4:0] inADDSUB,
  output outADDSUB
);

  wire not_1_out, not_2_out, not_3_out;

  not not_1 (not_1_out, inADDSUB[4]);
  not not_2 (not_2_out, inADDSUB[3]);
  not not_3 (not_3_out, inADDSUB[2]);
  and and_1 (outADDSUB, not_1_out, not_2_out, not_3_out, inADDSUB[1], inADDSUB[0]);
endmodule

module is_SHIFT (
  input  [2:0] inSHIFT,
  output outSHIFT
);

  wire not_1_out, not_2_out, not_3_out;

  not not_1 (not_1_out, inSHIFT[2]);
  not not_2 (not_2_out, inSHIFT[1]);
  not not_3 (not_3_out, inSHIFT[0]);
  and and_1 (outSHIFT, not_1_out, not_2_out, not_3_out);
endmodule

module use_IMM3 (
  input  is_ADD_SUB,
  input  is_10thBit,
  output outIsIMM3
);

  and and_1 (outIsIMM3, is_ADD_SUB, is_10thBit);
endmodule
